# Fritzing sketch FritzingSketch (saved by Fritzing 0.9.3b)
breadboards: 1

parts:
  Componente1 = Arduino Board Ethernet
  VCC1 = Battery
  U1 = Module 4 Relais 5V [package="Module 4 Relais 5V"]
  M1 = DC Motor  # not connected
  M2 = DC Motor  # not connected
  M3 = DC Motor  # not connected
  M5 = DC Motor

nets:
  N1: Componente1.D2_PWM, U1.IN4
  N2: Componente1.D3_PWM, U1.IN3
  N3: Componente1.D4, U1.IN2
  N4: Componente1.D5_PWM, U1.IN1
  N5: VCC1.-, U1.GND, M5.pin_1
  N6: VCC1.+, U1.VCC, U1.K1-NF

custom parts:
  Module 4 Relais 5V: Module 4 Relais 5V 4x SPD-06VDC-SD-C
